# Fritzing sketch 1.2 boca robô (saved by Fritzing 0.9.3b)
breadboards: 1

parts:
  Componente1 = Arduino Uno (Rev3)
  S1 = Momentary Switch [package=ksa_sealed_tac_switch]
  J1 = Basic Servo

nets:
  GND: Componente1.GND, S1.2, J1.gnd
  N1: Componente1.D1/TX, S1.4
  N2: Componente1.D5_PWM, J1.pulse
  5V: Componente1.5V, J1.vcc
