# Fritzing sketch 2.2 cabeca robô (saved by Fritzing 0.9.3b)
breadboards: 1

parts:
  Componente1 = Arduino Uno (Rev3)
  S1 = Momentary Switch [package=ksa_sealed_tac_switch]
  J1 = Basic Servo
  J2 = Basic Servo
  S2 = Momentary Switch [package=ksa_sealed_tac_switch]

nets:
  N1: Componente1.D1/TX, S1.4
  N2: Componente1.D2, S2.4
  N3: Componente1.D5_PWM, J1.pulse
  N4: Componente1.D6_PWM, J2.pulse
  VCC: Componente1.5V, J1.vcc, J2.vcc
  GND: Componente1.GND, S1.2, J1.gnd, J2.gnd, S2.2
