# Fritzing sketch 4.1 propulsor robô (saved by Fritzing 0.9.3b)
breadboards: 1

parts:
  Componente1 = Arduino Uno (Rev3)
  S1 = Momentary Switch [package=ksa_sealed_tac_switch]
  J1 = Basic Servo
  J2 = Basic Servo
  S2 = Momentary Switch [package=ksa_sealed_tac_switch]
  S3 = Momentary Switch [package=ksa_sealed_tac_switch]
  LED1 = LED - 5mm [color="Red (633nm)" package="5 mm [THT]"]
  R1 = Resistor [tolerance=±5% resistance=220 package=THT]
  LED2 = LED - 5mm [color="Red (633nm)" package="5 mm [THT]"]
  R2 = Resistor [tolerance=±5% resistance=220 package=THT]
  LED3 = LED - 5mm [color="Red (633nm)" package="5 mm [THT]"]

nets:
  N1: Componente1.D1/TX, S1.4
  N2: Componente1.D2, S2.4
  N3: Componente1.D3_PWM, S3.4
  N4: Componente1.D5_PWM, J1.pulse
  N5: Componente1.D6_PWM, J2.pulse
  N6: Componente1.D7, LED1.anode, LED2.anode
  5V: Componente1.5V, J1.vcc
  GND: Componente1.GND, S1.2, J1.gnd, S2.2, S3.2, R1.Pin_1, R2.Pin_0
  N7: LED1.cathode, R1.Pin_0, LED2.cathode
  N8: R2.Pin_1, LED3.cathode
